# Fritzing sketch TableSoccer (saved by Fritzing 0.9.0b)
breadboards: 2

parts:
  Part1 = Arduino Uno (Rev3) - ICSP
  S1 = Pushbutton [package="[THT]"]
  R2 = Resistor [tolerance=±5% resistance=330 package=THT]
  S2 = Pushbutton [package="[THT]"]
  S3 = Pushbutton [package="[THT]"]
  S4 = Pushbutton [package="[THT]"]
  R3 = Resistor [tolerance=±5% resistance=2.2k package=THT]
  R4 = Resistor [tolerance=±5% resistance=1k package=THT]
  R5 = Resistor [tolerance=±5% resistance=10 package=THT]
  R6 = Resistor [tolerance=±5% resistance=3.9k package=THT]
  LCD1 = LCD screen
  R7 = Trimmer Potentiometer [maximum_resistance=10kΩ package=THT]

nets:
  N1: Part1.A0, S1.Pin_3, S1.Pin_4, S2.Pin_3, S2.Pin_4, S3.Pin_3, S3.Pin_4, S4.Pin_3, S4.Pin_4, R6.Pin_1
  N2: Part1.D8, LCD1.E
  N3: Part1.D9_PWM, LCD1.DB4
  N4: Part1.D10_PWM/SS, LCD1.DB5
  N5: Part1.D11_PWM/MOSI, LCD1.DB6
  N6: Part1.D12/MISO, LCD1.DB7
  N7: Part1.D7, LCD1.RS
  5V: Part1.5V, R2.Pin_0, R3.Pin_1, R4.Pin_1, R5.Pin_1, LCD1.VDD, LCD1.LED+, R7.leg1
  GND: Part1.GND, R6.Pin_0, LCD1.VSS, LCD1.R/W, LCD1.LED-, R7.leg2
  N8: S1.Pin_1, S1.Pin_2, R2.Pin_1
  N9: S2.Pin_1, S2.Pin_2, R3.Pin_0
  N10: S3.Pin_1, S3.Pin_2, R4.Pin_0
  N11: S4.Pin_1, S4.Pin_2, R5.Pin_0
  N12: LCD1.V0, R7.wiper

notes:
  Why is 10ohm not enough?
